// Digital circuit CTRLUNIT.dig as structural Verilog
module CTRLUNIT (
  input  [7:0] OPC,
  input  Z,
  input  C,
  input  N,
  input  V,
  input  nMPC_RST,
  input  nHALT,
  input  CLK,
  input  nRST,
  output [15:0] C0_15,
  output [15:0] C16_31,
  output [15:0] C32_47
);

  wire _7408_1_pin3;
  wire [3:0] _74163_1_pin14;

  _7408 _7408_1 (
    .pin1(nRST), .pin2(nMPC_RST), .pin3(_7408_1_pin3), .pin4(1'b0), .pin5(1'b0), .pin7(1'b0), .pin9(1'b0),
    .pin10(1'b0), .pin12(1'b0), .pin13(1'b0), .pin14(1'b1));  // open: pin6, pin8, pin11
  _74163 _74163_1 (
    .pin1(_7408_1_pin3), .pin2(CLK), .pin3(1'b0), .pin4(1'b0), .pin5(1'b0), .pin6(1'b0), .pin7(nHALT),
    .pin8(1'b0), .pin9(1'b1), .pin10(nHALT), .pin11(_74163_1_pin14[3]), .pin12(_74163_1_pin14[2]),
    .pin13(_74163_1_pin14[1]), .pin14(_74163_1_pin14[0]), .pin16(1'b1));  // open: pin15
  ROM #(.AddrBits(16), .Bits(16)) _1ROM (.A({V, N, C, Z, _74163_1_pin14, OPC}), .sel(nRST), .D(C0_15));
  ROM #(.AddrBits(16), .Bits(16)) _2ROM (.A({V, N, C, Z, _74163_1_pin14, OPC}), .sel(nRST), .D(C16_31));
  ROM #(.AddrBits(16), .Bits(16)) _3ROM (.A({V, N, C, Z, _74163_1_pin14, OPC}), .sel(nRST), .D(C32_47));
  PullDown pulldown_1 (.out(C0_15[0]));
  PullUp pullup_1 (.out(C0_15[1]));
  PullDown pulldown_2 (.out(C16_31[0]));
  PullDown pulldown_3 (.out(C16_31[1]));
  PullUp pullup_2 (.out(C32_47[1]));
  PullDown pulldown_4 (.out(C32_47[0]));
  PullDown pulldown_5 (.out(C0_15[2]));
  PullUp pullup_3 (.out(C0_15[3]));
  PullUp pullup_4 (.out(C0_15[4]));
  PullUp pullup_5 (.out(C0_15[5]));
  PullDown pulldown_6 (.out(C16_31[2]));
  PullDown pulldown_7 (.out(C16_31[4]));
  PullUp pullup_6 (.out(C16_31[3]));
  PullUp pullup_7 (.out(C16_31[5]));
  PullDown pulldown_8 (.out(C32_47[2]));
  PullUp pullup_8 (.out(C32_47[3]));
  PullUp pullup_9 (.out(C32_47[4]));
  PullUp pullup_10 (.out(C32_47[5]));
  PullUp pullup_11 (.out(C0_15[6]));
  PullUp pullup_12 (.out(C0_15[7]));
  PullUp pullup_13 (.out(C0_15[8]));
  PullUp pullup_14 (.out(C0_15[9]));
  PullDown pulldown_9 (.out(C16_31[6]));
  PullDown pulldown_10 (.out(C16_31[7]));
  PullDown pulldown_11 (.out(C16_31[8]));
  PullDown pulldown_12 (.out(C16_31[9]));
  PullDown pulldown_13 (.out(C32_47[7]));
  PullDown pulldown_14 (.out(C32_47[9]));
  PullUp pullup_15 (.out(C32_47[6]));
  PullUp pullup_16 (.out(C32_47[8]));
  PullDown pulldown_15 (.out(C0_15[10]));
  PullDown pulldown_16 (.out(C0_15[11]));
  PullUp pullup_17 (.out(C0_15[12]));
  PullUp pullup_18 (.out(C0_15[13]));
  PullDown pulldown_17 (.out(C16_31[11]));
  PullDown pulldown_18 (.out(C16_31[13]));
  PullUp pullup_19 (.out(C16_31[10]));
  PullUp pullup_20 (.out(C16_31[12]));
  PullDown pulldown_19 (.out(C32_47[10]));
  PullDown pulldown_20 (.out(C32_47[11]));
  PullDown pulldown_21 (.out(C32_47[12]));
  PullDown pulldown_22 (.out(C32_47[13]));
  PullUp pullup_21 (.out(C0_15[14]));
  PullUp pullup_22 (.out(C0_15[15]));
  PullUp pullup_23 (.out(C16_31[14]));
  PullUp pullup_24 (.out(C16_31[15]));
  PullDown pulldown_23 (.out(C32_47[14]));
  PullDown pulldown_24 (.out(C32_47[15]));

  // Notes on the sheet:
  //   contents of _1ROM (hex, n*v repeats v):
  //   256*f7da,8*f1bb,8*f1fb,e1bb,d1bb,71fb,71fb,4*f1fb,e1fb,d1fb,6*f1fb
  //   ,8*f47f,8*b5ff,8*f5ff,8*f87f,8*b9ff,16*f9ff,8*f3ff,8*f1fb,8*f1bb
  //   ,32*f1fb,8*f1bb,16*f1fb,16*f1bb,24*f1fb,8*f1bb,f3fb,d3bb,f3fb
  //   ,d3bb,f3fb,d3bb,f3fb,d3bb,f1fb,f1fd,f1fb,f1fd,f1fb,f1fd,f1fb,f1fd
  //   ,d3bb,d3bb,b1fd,f1fd,f3fb,f3fb,f1fb,f1fb,b1ff,e3fb,f1ff,6*f1fb
  //   ,f3ff,f1fb,f1fb,f1fb,f9ff,f3ff,f1fb,88*f3fa,8*f5fe,120*f3fa,f1fb
  //   ,f7da,f1fb,f7da,f1fb,f7da,f1fb,f7da,8*f3fa,f7da,f7da,f3fa,f3fa
  //   ,fbee,fbee,f3fa,f3fa,f3fa,d1fa,7*f3fa,e7fe,4*f3fa,f5fe,217*f3fa
  //   ,8*e3bb,8*f3fa,e3ba,e3bb,f3fa,f3fa,fbf6,fbf6,11*f3fa,d7fe,222*f3fa
  //   ,8*b1fc,8*f3fa,b1fc,fbee,f3fa,f3fa,b1fc,f1fc,11*f3fa,b1fc,239*f3fa
  //   ,fbf6,255*f3fa,b1fc,2326*f3fa,256*f7da,8*f1bb,8*f1fb,e1bb,d1bb
  //   ,71fb,71fb,4*f1fb,e1fb,d1fb,6*f1fb,8*f47f,8*b5ff,8*f5ff,8*f87f
  //   ,8*b9ff,16*f9ff,8*f3ff,8*f1fb,8*f1bb,32*f1fb,8*f1bb,16*f1fb,16*f1bb
  //   ,24*f1fb,8*f1bb,f3fb,d3bb,d3bb,f3fb,f3fb,d3bb,f3fb,d3bb,f1fb,f1fd,f1fd
  //   ,f1fb,f1fb,f1fd,f1fb,f1fd,d3bb,d3bb,b1fd,f1fd,f3fb,f3fb,f1fb,f1fb
  //   ,b1ff,e3fb,f1ff,6*f1fb,f3ff,f1fb,f1fb,f1fb,f9ff,f3ff,f1fb,88*f3fa
  //   ,8*f5fe,120*f3fa,f1fb,f7da,f7da,f1fb,f1fb,f7da,f1fb,f7da,8*f3fa
  //   ,f7da,f7da,f3fa,f3fa,fbee,fbee,f3fa,f3fa,f3fa,d1fa,7*f3fa,e7fe
  //   ,4*f3fa,f5fe,217*f3fa,8*e3bb,8*f3fa,e3ba,e3bb,f3fa,f3fa,fbf6,fbf6
  //   ,11*f3fa,d7fe,222*f3fa,8*b1fc,8*f3fa,b1fc,fbee,f3fa,f3fa,b1fc
  //   ,f1fc,11*f3fa,b1fc,239*f3fa,fbf6,255*f3fa,b1fc,2326*f3fa,256*f7da
  //   ,8*f1bb,8*f1fb,e1bb,d1bb,71fb,71fb,4*f1fb,e1fb,d1fb,6*f1fb,8*f47f
  //   ,8*b5ff,8*f5ff,8*f87f,8*b9ff,16*f9ff,8*f3ff,8*f1fb,8*f1bb,32*f1fb
  //   ,8*f1bb,16*f1fb,16*f1bb,24*f1fb,8*f1bb,d3bb,f3fb,f3fb,d3bb,f3fb
  //   ,d3bb,f3fb,d3bb,f1fd,f1fb,f1fb,f1fd,f1fb,f1fd,f1fb,f1fd,d3bb,d3bb
  //   ,b1fd,f1fd,f3fb,f3fb,f1fb,f1fb,b1ff,e3fb,f1ff,6*f1fb,f3ff,f1fb,f1fb,f1fb
  //   ,f9ff,f3ff,f1fb,88*f3fa,8*f5fe,120*f3fa,f7da,f1fb,f1fb,f7da,f1fb
  //   ,f7da,f1fb,f7da,8*f3fa,f7da,f7da,f3fa,f3fa,fbee,fbee,f3fa,f3fa,f3fa
  //   ,d1fa,7*f3fa,e7fe,4*f3fa,f5fe,217*f3fa,8*e3bb,8*f3fa,e3ba,e3bb
  //   ,f3fa,f3fa,fbf6,fbf6,11*f3fa,d7fe,222*f3fa,8*b1fc,8*f3fa,b1fc
  //   ,fbee,f3fa,f3fa,b1fc,f1fc,11*f3fa,b1fc,239*f3fa,fbf6,255*f3fa
  //   ,b1fc,2326*f3fa,256*f7da,8*f1bb,8*f1fb,e1bb,d1bb,71fb,71fb,4*f1fb
  //   ,e1fb,d1fb,6*f1fb,8*f47f,8*b5ff,8*f5ff,8*f87f,8*b9ff,16*f9ff,8*f3ff
  //   ,8*f1fb,8*f1bb,32*f1fb,8*f1bb,16*f1fb,16*f1bb,24*f1fb,8*f1bb,d3bb
  //   ,f3fb,d3bb,f3fb,f3fb,d3bb,f3fb,d3bb,f1fd,f1fb,f1fd,f1fb,f1fb,f1fd
  //   ,f1fb,f1fd,d3bb,d3bb,b1fd,f1fd,f3fb,f3fb,f1fb,f1fb,b1ff,e3fb,f1ff
  //   ,6*f1fb,f3ff,f1fb,f1fb,f1fb,f9ff,f3ff,f1fb,88*f3fa,8*f5fe,120*f3fa
  //   ,f7da,f1fb,f7da,f1fb,f1fb,f7da,f1fb,f7da,8*f3fa,f7da,f7da,f3fa,f3fa
  //   ,fbee,fbee,f3fa,f3fa,f3fa,d1fa,7*f3fa,e7fe,4*f3fa,f5fe,217*f3fa
  //   ,8*e3bb,8*f3fa,e3ba,e3bb,f3fa,f3fa,fbf6,fbf6,11*f3fa,d7fe,222*f3fa
  //   ,8*b1fc,8*f3fa,b1fc,fbee,f3fa,f3fa,b1fc,f1fc,11*f3fa,b1fc,239*f3fa
  //   ,fbf6,255*f3fa,b1fc,2326*f3fa,256*f7da,8*f1bb,8*f1fb,e1bb,d1bb
  //   ,71fb,71fb,4*f1fb,e1fb,d1fb,6*f1fb,8*f47f,8*b5ff,8*f5ff,8*f87f
  //   ,8*b9ff,16*f9ff,8*f3ff,8*f1fb,8*f1bb,32*f1fb,8*f1bb,16*f1fb,16*f1bb
  //   ,24*f1fb,8*f1bb,f3fb,d3bb,f3fb,d3bb,d3bb,f3fb,f3fb,d3bb,f1fb,f1fd
  //   ,f1fb,f1fd,f1fd,f1fb,f1fb,f1fd,d3bb,d3bb,b1fd,f1fd,f3fb,f3fb,f1fb,f1fb
  //   ,b1ff,e3fb,f1ff,6*f1fb,f3ff,f1fb,f1fb,f1fb,f9ff,f3ff,f1fb,88*f3fa
  //   ,8*f5fe,120*f3fa,f1fb,f7da,f1fb,f7da,f7da,f1fb,f1fb,f7da,8*f3fa
  //   ,f7da,f7da,f3fa,f3fa,fbee,fbee,f3fa,f3fa,f3fa,d1fa,7*f3fa,e7fe
  //   ,4*f3fa,f5fe,217*f3fa,8*e3bb,8*f3fa,e3ba,e3bb,f3fa,f3fa,fbf6,fbf6
  //   ,11*f3fa,d7fe,222*f3fa,8*b1fc,8*f3fa,b1fc,fbee,f3fa,f3fa,b1fc
  //   ,f1fc,11*f3fa,b1fc,239*f3fa,fbf6,255*f3fa,b1fc,2326*f3fa,256*f7da
  //   ,8*f1bb,8*f1fb,e1bb,d1bb,71fb,71fb,4*f1fb,e1fb,d1fb,6*f1fb,8*f47f
  //   ,8*b5ff,8*f5ff,8*f87f,8*b9ff,16*f9ff,8*f3ff,8*f1fb,8*f1bb,32*f1fb
  //   ,8*f1bb,16*f1fb,16*f1bb,24*f1fb,8*f1bb,f3fb,d3bb,d3bb,f3fb,d3bb
  //   ,f3fb,f3fb,d3bb,f1fb,f1fd,f1fd,f1fb,f1fd,f1fb,f1fb,f1fd,d3bb,d3bb
  //   ,b1fd,f1fd,f3fb,f3fb,f1fb,f1fb,b1ff,e3fb,f1ff,6*f1fb,f3ff,f1fb,f1fb,f1fb
  //   ,f9ff,f3ff,f1fb,88*f3fa,8*f5fe,120*f3fa,f1fb,f7da,f7da,f1fb,f7da
  //   ,f1fb,f1fb,f7da,8*f3fa,f7da,f7da,f3fa,f3fa,fbee,fbee,f3fa,f3fa,f3fa
  //   ,d1fa,7*f3fa,e7fe,4*f3fa,f5fe,217*f3fa,8*e3bb,8*f3fa,e3ba,e3bb
  //   ,f3fa,f3fa,fbf6,fbf6,11*f3fa,d7fe,222*f3fa,8*b1fc,8*f3fa,b1fc
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  //   contents of _2ROM (hex, n*v repeats v):
  //   256*d428,8*d42a,8*d42e,d428,d428,d428,d429,d420,d430,d428,d428
  //   ,d42c,d42c,6*d428,16*d42a,8*d40a,16*d42c,8*d40c,8*d42c,8*d428
  //   ,8*55ee,8*55ea,8*55ee,8*5d6e,8*556e,8*576e,8*576a,8*56ee,8*566e
  //   ,8*5dea,8*556a,16*c42a,8*5d2c,8*5d28,9*d428,d408,d428,d408,d428
  //   ,d408,d428,d408,d428,d428,d428,d408,6*d428,d408,d428,d428,d428
  //   ,d42a,d42a,5*d428,9428,90*d428,8*d42a,158*d428,5428,494*d428,d408
  //   ,3090*d428,8*d42a,8*d42e,d428,d428,d428,d429,d420,d430,d428,d428
  //   ,d42c,d42c,6*d428,16*d42a,8*d40a,16*d42c,8*d40c,8*d42c,8*d428
  //   ,8*55ee,8*55ea,8*55ee,8*5d6e,8*556e,8*576e,8*576a,8*56ee,8*566e
  //   ,8*5dea,8*556a,16*c42a,8*5d2c,8*5d28,9*d428,d408,d408,d428,d428
  //   ,d408,d428,d408,d428,d428,d428,d408,6*d428,d408,d428,d428,d428
  //   ,d42a,d42a,5*d428,9428,90*d428,8*d42a,158*d428,5428,494*d428,d408
  //   ,3090*d428,8*d42a,8*d42e,d428,d428,d428,d429,d420,d430,d428,d428
  //   ,d42c,d42c,6*d428,16*d42a,8*d40a,16*d42c,8*d40c,8*d42c,8*d428
  //   ,8*55ee,8*55ea,8*5dee,16*5d6e,8*576e,8*576a,8*56ee,8*566e,8*5dea
  //   ,8*556a,16*c42a,8*5d2c,8*5d28,8*d428,d408,d428,d428,d408,d428
  //   ,d408,d428,d408,d428,d428,d428,d408,6*d428,d408,d428,d428,d428
  //   ,d42a,d42a,5*d428,9428,90*d428,8*d42a,158*d428,5428,494*d428,d408
  //   ,3090*d428,8*d42a,8*d42e,d428,d428,d428,d429,d420,d430,d428,d428
  //   ,d42c,d42c,6*d428,16*d42a,8*d40a,16*d42c,8*d40c,8*d42c,8*d428
  //   ,8*55ee,8*55ea,8*5dee,16*5d6e,8*576e,8*576a,8*56ee,8*566e,8*5dea
  //   ,8*556a,16*c42a,8*5d2c,8*5d28,8*d428,d408,d428,d408,d428,d428
  //   ,d408,d428,d408,d428,d428,d428,d408,6*d428,d408,d428,d428,d428
  //   ,d42a,d42a,5*d428,9428,90*d428,8*d42a,158*d428,5428,494*d428,d408
  //   ,3090*d428,8*d42a,8*d42e,d428,d428,d428,d429,d420,d430,d428,d428
  //   ,d42c,d42c,6*d428,16*d42a,8*d40a,16*d42c,8*d40c,8*d42c,8*d428
  //   ,8*55ee,8*55ea,8*55ee,8*5d6e,8*556e,8*576e,8*576a,8*56ee,8*566e
  //   ,8*5dea,8*556a,16*c42a,8*5d2c,8*5d28,9*d428,d408,d428,d408,d408
  //   ,d428,d428,d408,d428,d428,d428,d408,6*d428,d408,d428,d428,d428
  //   ,d42a,d42a,5*d428,9428,90*d428,8*d42a,158*d428,5428,494*d428,d408
  //   ,3090*d428,8*d42a,8*d42e,d428,d428,d428,d429,d420,d430,d428,d428
  //   ,d42c,d42c,6*d428,16*d42a,8*d40a,16*d42c,8*d40c,8*d42c,8*d428
  //   ,8*55ee,8*55ea,8*55ee,8*5d6e,8*556e,8*576e,8*576a,8*56ee,8*566e
  //   ,8*5dea,8*556a,16*c42a,8*5d2c,8*5d28,9*d428,d408,d408,d428,d408
  //   ,d428,d428,d408,d428,d428,d428,d408,6*d428,d408,d428,d428,d428
  //   ,d42a,d42a,5*d428,9428,90*d428,8*d42a,158*d428,5428,494*d428,d408
  //   ,3090*d428,8*d42a,8*d42e,d428,d428,d428,d429,d420,d430,d428,d428
  //   ,d42c,d42c,6*d428,16*d42a,8*d40a,16*d42c,8*d40c,8*d42c,8*d428
  //   ,8*55ee,8*55ea,8*5dee,16*5d6e,8*576e,8*576a,8*56ee,8*566e,8*5dea
  //   ,8*556a,16*c42a,8*5d2c,8*5d28,8*d428,d408,d428,d428,d408,d408
  //   ,d428,d428,d408,d428,d428,d428,d408,6*d428,d408,d428,d428,d428
  //   ,d42a,d42a,5*d428,9428,90*d428,8*d42a,158*d428,5428,494*d428,d408
  //   ,3090*d428,8*d42a,8*d42e,d428,d428,d428,d429,d420,d430,d428,d428
  //   ,d42c,d42c,6*d428,16*d42a,8*d40a,16*d42c,8*d40c,8*d42c,8*d428
  //   ,8*55ee,8*55ea,8*5dee,16*5d6e,8*576e,8*576a,8*56ee,8*566e,8*5dea
  //   ,8*556a,16*c42a,8*5d2c,8*5d28,8*d428,d408,d428,d408,d428,d408
  //   ,d428,d428,d408,d428,d428,d428,d408,6*d428,d408,d428,d428,d428
  //   ,d42a,d42a,5*d428,9428,90*d428,8*d42a,158*d428,5428,494*d428,d408
  //   ,3090*d428,8*d42a,8*d42e,d428,d428,d428,d429,d420,d430,d428,d428
  //   ,d42c,d42c,6*d428,16*d42a,8*d40a,16*d42c,8*d40c,8*d42c,8*d428
  //   ,8*55ee,8*55ea,8*55ee,8*5d6e,8*556e,8*576e,8*576a,8*56ee,8*566e
  //   ,8*5dea,8*556a,16*c42a,8*5d2c,8*5d28,9*d428,d408,d428,d408,d428
  //   ,d408,d408,4*d428,d408,6*d428,d408,d428,d428,d428,d42a,d42a,5*d428
  //   ,9428,90*d428,8*d42a,158*d428,5428,494*d428,d408,3090*d428,8*d42a
  //   ,8*d42e,d428,d428,d428,d429,d420,d430,d428,d428,d42c,d42c,6*d428
  //   ,16*d42a,8*d40a,16*d42c,8*d40c,8*d42c,8*d428,8*55ee,8*55ea,8*55ee
  //   ,8*5d6e,8*556e,8*576e,8*576a,8*56ee,8*566e,8*5dea,8*556a,16*c42a
  //   ,8*5d2c,8*5d28,9*d428,d408,d408,d428,d428,d408,d408,4*d428,d408
  //   ,6*d428,d408,d428,d428,d428,d42a,d42a,5*d428,9428,90*d428,8*d42a
  //   ,158*d428,5428,494*d428,d408,3090*d428,8*d42a,8*d42e,d428,d428,d428
  //   ,d429,d420,d430,d428,d428,d42c,d42c,6*d428,16*d42a,8*d40a,16*d42c
  //   ,8*d40c,8*d42c,8*d428,8*55ee,8*55ea,8*5dee,16*5d6e,8*576e,8*576a
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  //   contents of _3ROM (hex, n*v repeats v):
  //   312*17a,8*1fa,16*17a,8*16c,8*168,144*17a,172,15a,172,178,17c,17a
  //   ,13a,15a,17a,168,17a,17a,17a,16c,168,89*17a,8*16a,140*17a,16c,16c
  //   ,17a,17a,17a,13a,7*17a,168,4*17a,16a,7a,236*17a,16c,16c,11*17a
  //   ,16a,239*17a,16c,255*17a,16c,2894*17a,8*1fa,16*17a,8*16c,8*168
  //   ,144*17a,172,15a,172,178,17c,17a,13a,15a,17a,168,17a,17a,17a,16c
  //   ,168,89*17a,8*16a,140*17a,16c,16c,17a,17a,17a,13a,7*17a,168,4*17a
  //   ,16a,7a,236*17a,16c,16c,11*17a,16a,239*17a,16c,255*17a,16c,2894*17a
  //   ,8*1fa,16*17a,8*16c,8*168,144*17a,172,15a,172,178,17c,17a,13a
  //   ,15a,17a,168,17a,17a,17a,16c,168,89*17a,8*16a,140*17a,16c,16c
  //   ,17a,17a,17a,13a,7*17a,168,4*17a,16a,7a,236*17a,16c,16c,11*17a
  //   ,16a,239*17a,16c,255*17a,16c,2894*17a,8*1fa,16*17a,8*16c,8*168
  //   ,144*17a,172,15a,172,178,17c,17a,13a,15a,17a,168,17a,17a,17a,16c
  //   ,168,89*17a,8*16a,140*17a,16c,16c,17a,17a,17a,13a,7*17a,168,4*17a
  //   ,16a,7a,236*17a,16c,16c,11*17a,16a,239*17a,16c,255*17a,16c,2894*17a
  //   ,8*1fa,16*17a,8*16c,8*168,144*17a,172,15a,172,178,17c,17a,13a
  //   ,15a,17a,168,17a,17a,17a,16c,168,89*17a,8*16a,140*17a,16c,16c
  //   ,17a,17a,17a,13a,7*17a,168,4*17a,16a,7a,236*17a,16c,16c,11*17a
  //   ,16a,239*17a,16c,255*17a,16c,2894*17a,8*1fa,16*17a,8*16c,8*168
  //   ,144*17a,172,15a,172,178,17c,17a,13a,15a,17a,168,17a,17a,17a,16c
  //   ,168,89*17a,8*16a,140*17a,16c,16c,17a,17a,17a,13a,7*17a,168,4*17a
  //   ,16a,7a,236*17a,16c,16c,11*17a,16a,239*17a,16c,255*17a,16c,2894*17a
  //   ,8*1fa,16*17a,8*16c,8*168,144*17a,172,15a,172,178,17c,17a,13a
  //   ,15a,17a,168,17a,17a,17a,16c,168,89*17a,8*16a,140*17a,16c,16c
  //   ,17a,17a,17a,13a,7*17a,168,4*17a,16a,7a,236*17a,16c,16c,11*17a
  //   ,16a,239*17a,16c,255*17a,16c,2894*17a,8*1fa,16*17a,8*16c,8*168
  //   ,144*17a,172,15a,172,178,17c,17a,13a,15a,17a,168,17a,17a,17a,16c
  //   ,168,89*17a,8*16a,140*17a,16c,16c,17a,17a,17a,13a,7*17a,168,4*17a
  //   ,16a,7a,236*17a,16c,16c,11*17a,16a,239*17a,16c,255*17a,16c,2894*17a
  //   ,8*1fa,16*17a,8*16c,8*168,144*17a,172,15a,172,178,17c,17a,13a
  //   ,15a,17a,168,17a,17a,17a,16c,168,89*17a,8*16a,140*17a,16c,16c
  //   ,17a,17a,17a,13a,7*17a,168,4*17a,16a,7a,236*17a,16c,16c,11*17a
  //   ,16a,239*17a,16c,255*17a,16c,2894*17a,8*1fa,16*17a,8*16c,8*168
  //   ,144*17a,172,15a,172,178,17c,17a,13a,15a,17a,168,17a,17a,17a,16c
  //   ,168,89*17a,8*16a,140*17a,16c,16c,17a,17a,17a,13a,7*17a,168,4*17a
  //   ,16a,7a,236*17a,16c,16c,11*17a,16a,239*17a,16c,255*17a,16c,2894*17a
  //   ,8*1fa,16*17a,8*16c,8*168,144*17a,172,15a,172,178,17c,17a,13a
  //   ,15a,17a,168,17a,17a,17a,16c,168,89*17a,8*16a,140*17a,16c,16c
  //   ,17a,17a,17a,13a,7*17a,168,4*17a,16a,7a,236*17a,16c,16c,11*17a
  //   ,16a,239*17a,16c,255*17a,16c,2894*17a,8*1fa,16*17a,8*16c,8*168
  //   ,144*17a,172,15a,172,178,17c,17a,13a,15a,17a,168,17a,17a,17a,16c
  //   ,168,89*17a,8*16a,140*17a,16c,16c,17a,17a,17a,13a,7*17a,168,4*17a
  //   ,16a,7a,236*17a,16c,16c,11*17a,16a,239*17a,16c,255*17a,16c,2894*17a
  //   ,8*1fa,16*17a,8*16c,8*168,144*17a,172,15a,172,178,17c,17a,13a
  //   ,15a,17a,168,17a,17a,17a,16c,168,89*17a,8*16a,140*17a,16c,16c
  //   ,17a,17a,17a,13a,7*17a,168,4*17a,16a,7a,236*17a,16c,16c,11*17a
  //   ,16a,239*17a,16c,255*17a,16c,2894*17a,8*1fa,16*17a,8*16c,8*168
  //   ,144*17a,172,15a,172,178,17c,17a,13a,15a,17a,168,17a,17a,17a,16c
  //   ,168,89*17a,8*16a,140*17a,16c,16c,17a,17a,17a,13a,7*17a,168,4*17a
  //   ,16a,7a,236*17a,16c,16c,11*17a,16a,239*17a,16c,255*17a,16c,2894*17a
  //   ,8*1fa,16*17a,8*16c,8*168,144*17a,172,15a,172,178,17c,17a,13a
  //   ,15a,17a,168,17a,17a,17a,16c,168,89*17a,8*16a,140*17a,16c,16c
  //   ,17a,17a,17a,13a,7*17a,168,4*17a,16a,7a,236*17a,16c,16c,11*17a
  //   ,16a,239*17a,16c,255*17a,16c,2894*17a,8*1fa,16*17a,8*16c,8*168
  //   ,144*17a,172,15a,172,178,17c,17a,13a,15a,17a,168,17a,17a,17a,16c
  //   ,168,89*17a,8*16a,140*17a,16c,16c,17a,17a,17a,13a,7*17a,168,4*17a
  //   ,16a,7a,236*17a,16c,16c,11*17a,16a,239*17a,16c,255*17a,16c,2582*17a
endmodule
